# Fritzing sketch lidar-pcb1 (saved by Fritzing 0.9.3b)
circuit board: 5cm x 5cm
breadboards: 1

parts:
  Part1 = Arduino Nano (Rev3.0) (ICSP)
  Pololu_A1 = Pololu A4988 [package=SO16]
  J2 = screw terminal, 3 pins
  J3 = screw terminal, 4 pins
  C3 = Electrolytic Capacitor [capacitance=100µF package="100 mil [THT, electrolytic]"]
  JP1 = Header 2 [package=screwterminal-3.5mm-2_lock]
  J4 = screw terminal, 5 pins
  JP2 = Header 2 [package=screwterminal-3.5mm-2_lock]
  C4 = Electrolytic Capacitor [capacitance=1µF package="100 mil [THT, electrolytic]"]
  Q1 = PNP-Transistor [package="TO92 [THT]"]
  C5 = Ceramic Capacitor [capacitance=100nF package="100 mil [THT, multilayer]"]
  C6 = Ceramic Capacitor [capacitance=100nF package="100 mil [THT, multilayer]"]

nets (from the pcb view):
  GND: Part1.GND, Pololu_A1.GND, J2.pin1, C3.-, JP1.1, J4.pin1, J4.pin2, J4.pin3, JP2.1, C4.-, Q1.E, Q1.B, C5.0, C5.1, C6.0
  N1: Part1.D2, Pololu_A1.DIR
  N2: Part1.D3, Pololu_A1.RESET, Pololu_A1.SLEEP
  N3: Part1.D4, Pololu_A1.ENABLE
  N4: Part1.D5, J2.pin2
  5V: Part1.5V, Pololu_A1.VDD, J2.pin3, JP2.2, C4.+
  N5: Part1.A5, J4.pin4
  N6: Part1.A4, J4.pin5
  N7: Pololu_A1.1B, J3.pin4
  N8: Pololu_A1.1A, J3.pin3
  N9: Pololu_A1.2A, J3.pin2
  N10: Pololu_A1.2B, J3.pin1
  N11: Pololu_A1.VMOT, C3.+, JP1.2, Q1.C, C6.1
